# Fritzing sketch Circuit (saved by Fritzing 0.9.3b)
breadboards: 1

parts:
  Part1 = KY-003 Hall Magnetic Sensor Module [package="Breakout board"]
  Composant1 = Arduino Nano (Rev3.0) (ICSP)
  U1 = POT [package=pot_alpha_rv16af-20]
  R1 = Resistor [tolerance=±5% resistance=220 package="2512 [SMD]"]

nets:
  N1: Part1.S, Composant1.D2
  VIN: Part1.Vin, Composant1.5V, U1.A
  N2: Part1.-, Composant1.GND, R1.Pin_1
  N3: Composant1.A0, U1.S
  N4: U1.E, R1.Pin_0

custom parts:
  KY-003 Hall Magnetic Sensor Module: KEYES KY-003 Arduino Hall Magnetic Sensor Module is a switch that will turn on/off in the presence of a magnetic field.
